# Fritzing sketch Sketch (saved by Fritzing 0.9.4)
breadboards: 1

parts:
  Nano1 = Arduino Nano v2.3
  Часы = DS1307 [package=so08]
  Oled_0_96 = Grove OLED 128x96
  ENCODER1 = Rotary Encoder with switch (KY-040) [part_number=KY-040]
  LED1 = LED - 3mm [color="Red (633nm)" package="3 mm [THT]"]
  Buzzer = Piezo Speaker
  R1 = Resistor [tolerance=±5% resistance=220 package=THT]

nets:
  GND: Nano1.GND, Часы.GND, Oled_0_96.GND, ENCODER1.GND, ENCODER1.+, Buzzer.pin1, R1.Pin_1
  N1: Nano1.D2, ENCODER1.CLK
  N2: Nano1.D3, ENCODER1.SW
  N3: Nano1.D4, ENCODER1.DT
  N4: Nano1.D5, Buzzer.pin2
  N5: Nano1.D6, LED1.cathode
  N6: Nano1.A5, Часы.SCL, Oled_0_96.SDA
  N7: Nano1.A4, Часы.SDA, Oled_0_96.SCL
  5V: Часы.VCC, Oled_0_96.VCC
  N8: LED1.anode, R1.Pin_0

custom parts:
  Rotary Encoder with switch (KY-040): A Rotary Encoder with switch
